// Logisim project 2^n_mod5(new).circ as structural Verilog: 4 circuits, main circuit mod5
module mod5 (
  input  \input ,
  output out_2,
  output out_3,
  output out_4,
  output out_5,
  output out_6
);

  wire clock_1_out;
  wire [1:0] register_1_q, \状态转移_1_out_3 ;

  \状态转移  \u_状态转移_1  (.\input (\input ), .in_1(register_1_q), .out_3(\状态转移_1_out_3 ));
  Register #(.width(2)) register_1 (.D(\状态转移_1_out_3 ), .Q(register_1_q), .clk(clock_1_out));  // open: en, clr
  Clock clock_1 (.out(clock_1_out));
  \状态输出  \u_状态输出_1  (
    .in_1(register_1_q), .\input (\input ), .output0(out_2), .output1(out_3), .output2(out_4),
    .output3(out_5), .output4(out_6));
endmodule

module \状态转移  (
  input  [1:0] in_1,
  input  \input ,
  output [1:0] out_3
);

  wire and_1_out, and_2_out, and_3_out, and_4_out, and_5_out, and_6_out, not_1_out, not_2_out, not_3_out,
       not_4_out, not_5_out, not_6_out, not_7_out, not_8_out;

  not not_1 (not_1_out, in_1[1]);
  not not_2 (not_2_out, in_1[0]);
  not not_3 (not_3_out, in_1[1]);
  not not_4 (not_4_out, in_1[0]);
  not not_5 (not_5_out, in_1[1]);
  not not_6 (not_6_out, \input );
  not not_7 (not_7_out, in_1[0]);
  not not_8 (not_8_out, \input );
  and and_1 (and_1_out, not_1_out, in_1[0]);
  and and_2 (and_2_out, in_1[1], not_2_out);
  and and_3 (and_3_out, not_3_out, not_4_out, \input );
  and and_4 (and_4_out, not_5_out, in_1[0], not_6_out);
  and and_5 (and_5_out, in_1[1], not_7_out, not_8_out);
  and and_6 (and_6_out, in_1[1], in_1[0], \input );
  or or_1 (out_3[1], and_1_out, and_2_out);
  or or_2 (out_3[0], and_3_out, and_4_out, and_5_out, and_6_out);
endmodule

module \状态储存  (
  input  [1:0] in_1,
  input  clock,
  output [1:0] out_3
);

  Register #(.width(1)) register_1 (.D(in_1[0]), .Q(out_3[0]), .clk(clock));  // open: en, clr
  Register #(.width(1)) register_2 (.D(in_1[1]), .Q(out_3[1]), .clk(clock));  // open: en, clr
endmodule

module \状态输出  (
  input  [1:0] in_1,
  input  \input ,
  output output0,
  output output1,
  output output2,
  output output3,
  output output4
);

  wire and_1_out, and_2_out, and_3_out, and_4_out, and_5_out, and_6_out, and_7_out, and_8_out, not_1_out,
       not_2_out, not_3_out, not_4_out, not_5_out, not_6_out, not_7_out, not_8_out, not_9_out, not_10_out,
       not_11_out, not_12_out;

  not not_1 (not_1_out, in_1[1]);
  not not_2 (not_2_out, in_1[0]);
  not not_3 (not_3_out, \input );
  not not_4 (not_4_out, \input );
  not not_5 (not_5_out, in_1[1]);
  not not_6 (not_6_out, in_1[0]);
  not not_7 (not_7_out, in_1[1]);
  not not_8 (not_8_out, in_1[0]);
  not not_9 (not_9_out, in_1[1]);
  not not_10 (not_10_out, \input );
  not not_11 (not_11_out, in_1[0]);
  not not_12 (not_12_out, \input );
  and and_1 (and_1_out, not_1_out, not_2_out, not_3_out);
  and and_2 (and_2_out, in_1[1], in_1[0], not_4_out);
  and and_3 (and_3_out, not_5_out, not_6_out, \input );
  and and_4 (and_4_out, in_1[1], in_1[0], \input );
  and and_5 (and_5_out, not_7_out, in_1[0], \input );
  and and_6 (and_6_out, in_1[1], not_8_out, \input );
  and and_7 (and_7_out, not_9_out, in_1[0], not_10_out);
  and and_8 (and_8_out, in_1[1], not_11_out, not_12_out);
  or or_1 (output1, and_1_out, and_2_out);
  or or_2 (output2, and_3_out, and_4_out);
  or or_3 (output3, and_5_out, and_6_out);
  or or_4 (output4, and_7_out, and_8_out);

  assign output0 = 1'b0;
endmodule
