// Logisim project 2^n_mod5.circ as structural Verilog: 1 circuit, main circuit mod5
module mod5 (
  input  Input,
  output s0,
  output s1,
  output s2,
  output s3,
  output s4
);

  wire clock_1_out, register_1_q, register_2_q;
  wire [1:0] xor_2_out;

  xor xor_1 (xor_2_out[1], register_1_q, register_2_q);
  Clock clock_1 (.out(clock_1_out));
  ExactlyOne xor_2 (.out(xor_2_out[0]), .in0(register_1_q), .in2(Input), .in4(register_2_q));
  Register #(.width(1)) register_1 (.D(xor_2_out[1]), .en(1'b1), .Q(register_1_q), .clk(clock_1_out));  // open: clr
  Register #(.width(1)) register_2 (.D(xor_2_out[0]), .en(1'b1), .Q(register_2_q), .clk(clock_1_out));  // open: clr
  Demultiplexer #(.select(2), .disabled(0), .enable("false")) demultiplexer_1 (
    .out0(s1), .out1(s2), .out2(s3), .out3(s4), .in(1'b1), .sel(xor_2_out));

  assign s0 = 1'b0;
endmodule
