// Logisim project CRC.circ as structural Verilog: 3 circuits, main circuit CRC
module CRC (
  input  [7:0] A,
  input  [3:0] B,
  output [10:0] out_3
);

  wire [2:0] \模二除法器_1_三位余数 , \模二除法器_2_三位余数 , \模二除法器_3_三位余数 , \模二除法器_4_三位余数 , \模二除法器_5_三位余数 , \模二除法器_6_三位余数 ,
       \模二除法器_7_三位余数 ;
  wire [3:0] \n3_1器_1_out_3 , \n3_1器_2_out_3 , \n3_1器_3_out_3 , \n3_1器_4_out_3 , \n3_1器_5_out_3 ,
       \n3_1器_6_out_3 , \n3_1器_7_out_3 ;

  // Probe on {A, 3'b000}
  \模二除法器  \u_模二除法器_1  (.\被除数 (A[7:4]), .\除数 (B), .\三位余数 (\模二除法器_1_三位余数 ));  // open: 商
  \_3_1器  \u_3_1器_1  (._3(\模二除法器_1_三位余数 ), ._1(A[3]), .out_3(\n3_1器_1_out_3 ));
  \模二除法器  \u_模二除法器_2  (.\被除数 (\n3_1器_1_out_3 ), .\除数 (B), .\三位余数 (\模二除法器_2_三位余数 ));  // open: 商
  \_3_1器  \u_3_1器_2  (._3(\模二除法器_2_三位余数 ), ._1(A[2]), .out_3(\n3_1器_2_out_3 ));
  \模二除法器  \u_模二除法器_3  (.\被除数 (\n3_1器_2_out_3 ), .\除数 (B), .\三位余数 (\模二除法器_3_三位余数 ));  // open: 商
  \_3_1器  \u_3_1器_3  (._3(\模二除法器_3_三位余数 ), ._1(A[1]), .out_3(\n3_1器_3_out_3 ));
  \模二除法器  \u_模二除法器_4  (.\被除数 (\n3_1器_3_out_3 ), .\除数 (B), .\三位余数 (\模二除法器_4_三位余数 ));  // open: 商
  \_3_1器  \u_3_1器_4  (._3(\模二除法器_4_三位余数 ), ._1(A[0]), .out_3(\n3_1器_4_out_3 ));
  \模二除法器  \u_模二除法器_5  (.\被除数 (\n3_1器_4_out_3 ), .\除数 (B), .\三位余数 (\模二除法器_5_三位余数 ));  // open: 商
  \_3_1器  \u_3_1器_5  (._3(\模二除法器_5_三位余数 ), ._1(1'b0), .out_3(\n3_1器_5_out_3 ));
  \模二除法器  \u_模二除法器_6  (.\被除数 (\n3_1器_5_out_3 ), .\除数 (B), .\三位余数 (\模二除法器_6_三位余数 ));  // open: 商
  \_3_1器  \u_3_1器_6  (._3(\模二除法器_6_三位余数 ), ._1(1'b0), .out_3(\n3_1器_6_out_3 ));
  \模二除法器  \u_模二除法器_7  (.\被除数 (\n3_1器_6_out_3 ), .\除数 (B), .\三位余数 (\模二除法器_7_三位余数 ));  // open: 商
  \_3_1器  \u_3_1器_7  (._3(\模二除法器_7_三位余数 ), ._1(1'b0), .out_3(\n3_1器_7_out_3 ));
  \模二除法器  \u_模二除法器_8  (.\被除数 (\n3_1器_7_out_3 ), .\除数 (B), .\三位余数 (out_3[2:0]));  // open: 商

  assign out_3[10:3] = A;

  // Other names for the same wires on the sheet: bit3 = A[0]; bit4 = A[1]; bit5 = A[2]; bit6 = A[3];
  //   bit7_10[3:0] = A[7:4]; 除数[3:0] = B
endmodule

module \模二除法器  (
  input  [3:0] \被除数 ,
  input  [3:0] \除数 ,
  output \商 ,
  output [2:0] \三位余数 
);

  wire [3:0] xor_1_out;
  wire [3:3] multiplexer_1_out;

  assign xor_1_out = \被除数  ^ \除数 ;  // XOR_Gate xor_1, 4 bits wide
  Multiplexer #(.width(4)) multiplexer_1 (
    .in0(\被除数 ), .in1(xor_1_out), .out({multiplexer_1_out[3], \三位余数 }), .sel(\被除数 [3]));  // open: en

  assign \商  = \被除数 [3];

  // Other names for the same wires on the sheet: 被除数最高位 = \被除数 [3]
endmodule

module \_3_1器  (
  input  [2:0] _3,
  input  _1,
  output [3:0] out_3
);


  assign out_3 = {_3, _1};
endmodule
