// Logisim project Logisim_4bit_sort.circ as structural Verilog: 4 circuits, main circuit 1bit_swap
module _1bit_swap (
  input  input1,
  input  input2,
  input  on,
  output out_4,
  output out_5
);

  wire and_1_out, xor_1_out;

  xor xor_1 (xor_1_out, input1, input2);
  and and_1 (and_1_out, xor_1_out, on);
  xor xor_2 (out_4, input1, and_1_out);
  xor xor_3 (out_5, and_1_out, input2);
endmodule

module _4bit_sort (
  input  [3:0] in_1,
  input  [3:0] in_2,
  input  [3:0] in_3,
  input  [3:0] in_4,
  output [3:0] out_5,
  output [3:0] out_6,
  output [3:0] out_7,
  output [3:0] out_8
);

  wire [3:0] n4bit_cmp_sort2_1_out_3, n4bit_cmp_sort2_1_out_4, n4bit_cmp_sort2_2_out_3,
       n4bit_cmp_sort2_2_out_4, n4bit_cmp_sort2_3_out_3, n4bit_cmp_sort2_4_out_3, n4bit_cmp_sort2_4_out_4,
       n4bit_cmp_sort2_5_out_3;

  _4bit_cmp_sort2 u_4bit_cmp_sort2_1 (
    .in_1(in_1), .in_2(in_2), .out_3(n4bit_cmp_sort2_1_out_3), .out_4(n4bit_cmp_sort2_1_out_4));
  _4bit_cmp_sort2 u_4bit_cmp_sort2_2 (
    .in_1(n4bit_cmp_sort2_1_out_4), .in_2(in_3), .out_3(n4bit_cmp_sort2_2_out_3),
    .out_4(n4bit_cmp_sort2_2_out_4));
  _4bit_cmp_sort2 u_4bit_cmp_sort2_3 (
    .in_1(n4bit_cmp_sort2_2_out_4), .in_2(in_4), .out_3(n4bit_cmp_sort2_3_out_3), .out_4(out_8));
  _4bit_cmp_sort2 u_4bit_cmp_sort2_4 (
    .in_1(n4bit_cmp_sort2_1_out_3), .in_2(n4bit_cmp_sort2_2_out_3), .out_3(n4bit_cmp_sort2_4_out_3),
    .out_4(n4bit_cmp_sort2_4_out_4));
  _4bit_cmp_sort2 u_4bit_cmp_sort2_5 (
    .in_1(n4bit_cmp_sort2_4_out_4), .in_2(n4bit_cmp_sort2_3_out_3), .out_3(n4bit_cmp_sort2_5_out_3),
    .out_4(out_7));
  _4bit_cmp_sort2 u_4bit_cmp_sort2_6 (
    .in_1(n4bit_cmp_sort2_4_out_3), .in_2(n4bit_cmp_sort2_5_out_3), .out_3(out_5), .out_4(out_6));
endmodule

module _4bit_swap (
  input  [3:0] input1,
  input  [3:0] input2,
  input  on_off,
  output [3:0] output1,
  output [3:0] output2
);

  _1bit_swap u_1bit_swap_1 (
    .input1(input1[0]), .input2(input2[0]), .on(on_off), .out_4(output1[0]), .out_5(output2[0]));
  _1bit_swap u_1bit_swap_2 (
    .input1(input1[1]), .input2(input2[1]), .on(on_off), .out_4(output1[1]), .out_5(output2[1]));
  _1bit_swap u_1bit_swap_3 (
    .input1(input1[2]), .input2(input2[2]), .on(on_off), .out_4(output1[2]), .out_5(output2[2]));
  _1bit_swap u_1bit_swap_4 (
    .input1(input1[3]), .input2(input2[3]), .on(on_off), .out_4(output1[3]), .out_5(output2[3]));
endmodule

module _4bit_cmp_sort2 (
  input  [3:0] in_1,
  input  [3:0] in_2,
  output [3:0] out_3,
  output [3:0] out_4
);

  wire comparator_1_gt;

  Comparator #(.width(4), .mode("unsigned")) comparator_1 (.a(in_1), .b(in_2), .gt(comparator_1_gt));  // open: eq, lt
  _4bit_swap u_4bit_swap_1 (.input1(in_1), .input2(in_2), .on_off(comparator_1_gt), .output1(out_3), .output2(out_4));
endmodule
