// Logisim project P3_L0_weak_2023.circ as structural Verilog: 9 circuits, main circuit register_init
module register_init (
  input  [31:0] data_in,
  input  enable,
  input  reset,
  input  clock,
  output [31:0] \output 
);

  wire comparator_1_eq;
  wire [31:0] register_1_q;

  Register #(.width(32)) register_1 (.D(data_in), .en(enable), .Q(register_1_q), .clk(clock), .clr(reset));
  Comparator #(.width(32), .mode("unsigned")) comparator_1 (
    .a(register_1_q), .b({32{1'b0}}), .eq(comparator_1_eq));  // open: gt, lt
  Multiplexer #(.width(32)) multiplexer_1 (
    .in0(register_1_q), .in1(32'h3000), .out(\output ), .sel(comparator_1_eq));  // open: en
endmodule

module main (
  input  in_1,
  output [31:0] out_2,
  output [31:0] out_3,
  output out_4,
  output [4:0] out_5,
  output [31:0] out_6,
  output out_7,
  output [31:0] out_8,
  output [31:0] out_9
);

  wire ALU_cmp, ALUsrc, and_1_out, branch, clock, ImmExtend, Jump, Link, MemtoReg, RegDst;
  wire [2:0] ALUop;
  wire [4:0] multiplexer_1_out, rd, rs, rt, shamt;
  wire [5:0] func, option;
  wire [11:0] Address_changer_out_2;
  wire [15:0] immediate;
  wire [25:0] address;
  wire [27:0] bit_extender_2_out, jump_next_PC;
  wire [31:0] adder_2_out, multiplexer_3_out, multiplexer_5_out, multiplexer_6_out, multiplexer_7_out,
       next_PC, PC_4, RAM_data, RegRead1, shifter_1_out, sign_extent_offset, zero_extent_imm;

  Multiplexer #(.width(5)) multiplexer_1 (.in0(rt), .in1(rd), .out(multiplexer_1_out), .sel(RegDst));  // open: en
  assign sign_extent_offset = {{16{immediate[15]}}, immediate};  // Bit_Extender bit_extender_1
  Adder #(.width(32)) adder_1 (.a(32'h4), .b(out_3), .out(PC_4));  // open: cin, cout
  assign bit_extender_2_out = {{2{1'b0}}, address};  // Bit_Extender bit_extender_2
  Multiplexer #(.width(5)) multiplexer_2 (
    .in0(multiplexer_1_out), .in1({5{1'b1}}), .out(out_5), .sel(Link));  // open: en
  Shifter #(.width(32)) shifter_1 (.in(sign_extent_offset), .\dist (5'b00010), .out(shifter_1_out));
  Shifter #(.width(28)) shifter_2 (.in(bit_extender_2_out), .\dist (5'b00010), .out(jump_next_PC));
  GRF GRF (
    .WD3(out_6), .A3(out_5), .A1(rs), .A2(rt), .RD1(RegRead1), .RD2(out_9), .clk(clock), .reset(in_1),
    .WE3(out_4));
  RAM #(.addrWidth(12), .dataWidth(32), .bus("separate")) ram_1 (
    .addr(out_8[13:2]), .din(out_9), .data(RAM_data), .str(out_7), .clk(clock), .clr(in_1));  // open: sel, ld
  Adder #(.width(32)) adder_2 (.a(PC_4), .b(shifter_1_out), .out(adder_2_out));  // open: cin, cout
  assign zero_extent_imm = {{16{1'b0}}, immediate};  // Bit_Extender bit_extender_3
  Multiplexer #(.width(32)) multiplexer_3 (
    .in0(PC_4), .in1(adder_2_out), .out(multiplexer_3_out), .sel(and_1_out));  // open: en
  and and_1 (and_1_out, branch, ALU_cmp);
  Multiplexer #(.width(32)) multiplexer_4 (
    .in0(multiplexer_3_out), .in1({out_3[31:28], jump_next_PC}), .out(next_PC), .sel(Jump));  // open: en
  Multiplexer #(.width(32)) multiplexer_5 (
    .in0(out_9), .in1(multiplexer_6_out), .out(multiplexer_5_out), .sel(ALUsrc));  // open: en
  Multiplexer #(.width(32)) multiplexer_6 (
    .in0(zero_extent_imm), .in1(sign_extent_offset), .out(multiplexer_6_out), .sel(ImmExtend));  // open: en
  Comtrol_Unit comtrol_unit_1 (
    .option(option), .func(func), .RegWrite(out_4), .RegDst(RegDst), .ALUsrc(ALUsrc), .ALUop(ALUop),
    .Branch(branch), .MemWrite(out_7), .MemtoReg(MemtoReg), .ImmExtend(ImmExtend), .Jump(Jump), .Link(Link));
  // register_init Program_counter: pin names not known; wires that end beside it: next_PC, 32'h3000, clock, in_1, out_3
  // Probe on next_PC
  ALU alu_1 (.inputA(RegRead1), .inputB(multiplexer_5_out), .option(ALUop), .output_calc(out_8), .output_cmp(ALU_cmp));
  Multiplexer #(.width(32)) multiplexer_7 (
    .in0(out_8), .in1(RAM_data), .out(multiplexer_7_out), .sel(MemtoReg));  // open: en
  Multiplexer #(.width(32)) multiplexer_8 (.in0(multiplexer_7_out), .in1(PC_4), .out(out_6), .sel(Link));  // open: en
  address_changer Address_changer (.in_1(out_3), .out_2(Address_changer_out_2));
  ROM #(.addrWidth(12), .dataWidth(32)) rom_1 (.addr(Address_changer_out_2), .data(out_2));  // open: sel
  Instr_Splitter Instr_Splitter (
    .in_1(out_2), .immediate(immediate), .func(func), .shamt(shamt), .rd(rd), .rt(rt), .rs(rs),
    .option(option), .address(address));
  Clock clock_1 (.out(clock));

  // Other names for the same wires on the sheet: ALU_calc[31:0] = out_8; InStr[31:0] = out_2;
  //   jump_next_PC[31:28] = out_3[31:28]; PC[31:0] = out_3; MemWrite = out_7; offset[15:0] = immediate;
  //   RegAddress[4:0] = out_5; RegRead2[31:0] = out_9; RegWrite = out_4; reset = in_1; WriteValue[31:0] = out_6

  // Notes on the sheet:
  //   选择写入寄存器的序号
  //   下一指令地址计算
  //   地址偏移量符号拓展
  //   内存 Memory
  //   跳转指令计算
  //   寄存器堆 GRF
  //   立即数零拓展
  //   控制逻辑单元
  //   ALU 计算单元
  //   状态存取
  //   contents of rom_1 (hex, n*v repeats v):
  //   3c06007b 3c07ffff 34e8ffff 340a0008 34090001 1294820 112a0001 c000c05
endmodule

module GRF (
  input  clk,
  input  reset,
  input  WE3,
  input  [31:0] WD3,
  input  [4:0] A3,
  input  [4:0] A1,
  input  [4:0] A2,
  output [31:0] RD1,
  output [31:0] RD2
);

  wire [31:0] _0input, _0output, _1input, _1output, _2input, _2output, _3input, _3output, _4input, _4output,
       _5input, _5output, _6input, _6output, _7input, _7output, _8input, _8output, _9input, _9output,
       _10input, _10output, _11input, _11output, _12input, _12output, _13input, _13output, _14input,
       _14output, _15input, _15output, _16input, _16output, _17input, _17output, _18input, _18output,
       _19input, _19output, _20input, _20output, _21input, _21output, _22input, _22output, _23input,
       _23output, _24input, _24output, _25input, _25output, _26input, _26output, _27input, _27output,
       _28input, _28output, _29input, _29output, _30input, _30output, _31input, _31output;

  Register #(.width(32)) register_1 (.D(_0input), .en(1'b0), .Q(_0output), .clk(clk), .clr(reset));
  Register #(.width(32)) register_2 (.D(_1input), .en(WE3), .Q(_1output), .clk(clk), .clr(reset));
  Register #(.width(32)) register_3 (.D(_2input), .en(WE3), .Q(_2output), .clk(clk), .clr(reset));
  Register #(.width(32)) register_4 (.D(_3input), .en(WE3), .Q(_3output), .clk(clk), .clr(reset));
  Register #(.width(32)) register_5 (.D(_4input), .en(WE3), .Q(_4output), .clk(clk), .clr(reset));
  Register #(.width(32)) register_6 (.D(_5input), .en(WE3), .Q(_5output), .clk(clk), .clr(reset));
  Register #(.width(32)) register_7 (.D(_6input), .en(WE3), .Q(_6output), .clk(clk), .clr(reset));
  Register #(.width(32)) register_8 (.D(_7input), .en(WE3), .Q(_7output), .clk(clk), .clr(reset));
  Register #(.width(32)) register_9 (.D(_8input), .en(WE3), .Q(_8output), .clk(clk), .clr(reset));
  Register #(.width(32)) register_10 (.D(_9input), .en(WE3), .Q(_9output), .clk(clk), .clr(reset));
  Register #(.width(32)) register_11 (.D(_10input), .en(WE3), .Q(_10output), .clk(clk), .clr(reset));
  Register #(.width(32)) register_12 (.D(_11input), .en(WE3), .Q(_11output), .clk(clk), .clr(reset));
  Register #(.width(32)) register_13 (.D(_12input), .en(WE3), .Q(_12output), .clk(clk), .clr(reset));
  Register #(.width(32)) register_14 (.D(_13input), .en(WE3), .Q(_13output), .clk(clk), .clr(reset));
  Register #(.width(32)) register_15 (.D(_14input), .en(WE3), .Q(_14output), .clk(clk), .clr(reset));
  Register #(.width(32)) register_16 (.D(_15input), .en(WE3), .Q(_15output), .clk(clk), .clr(reset));
  Register #(.width(32)) register_17 (.D(_16input), .en(WE3), .Q(_16output), .clk(clk), .clr(reset));
  Register #(.width(32)) register_18 (.D(_17input), .en(WE3), .Q(_17output), .clk(clk), .clr(reset));
  Register #(.width(32)) register_19 (.D(_18input), .en(WE3), .Q(_18output), .clk(clk), .clr(reset));
  Register #(.width(32)) register_20 (.D(_19input), .en(WE3), .Q(_19output), .clk(clk), .clr(reset));
  Register #(.width(32)) register_21 (.D(_20input), .en(WE3), .Q(_20output), .clk(clk), .clr(reset));
  Register #(.width(32)) register_22 (.D(_21input), .en(WE3), .Q(_21output), .clk(clk), .clr(reset));
  Register #(.width(32)) register_23 (.D(_22input), .en(WE3), .Q(_22output), .clk(clk), .clr(reset));
  Register #(.width(32)) register_24 (.D(_23input), .en(WE3), .Q(_23output), .clk(clk), .clr(reset));
  Register #(.width(32)) register_25 (.D(_24input), .en(WE3), .Q(_24output), .clk(clk), .clr(reset));
  Register #(.width(32)) register_26 (.D(_25input), .en(WE3), .Q(_25output), .clk(clk), .clr(reset));
  Register #(.width(32)) register_27 (.D(_26input), .en(WE3), .Q(_26output), .clk(clk), .clr(reset));
  Register #(.width(32)) register_28 (.D(_27input), .en(WE3), .Q(_27output), .clk(clk), .clr(reset));
  Register #(.width(32)) register_29 (.D(_28input), .en(WE3), .Q(_28output), .clk(clk), .clr(reset));
  Register #(.width(32)) register_30 (.D(_29input), .en(WE3), .Q(_29output), .clk(clk), .clr(reset));
  Register #(.width(32)) register_31 (.D(_30input), .en(WE3), .Q(_30output), .clk(clk), .clr(reset));
  Register #(.width(32)) register_32 (.D(_31input), .en(WE3), .Q(_31output), .clk(clk), .clr(reset));
  Multiplexer #(.select(5), .width(32), .disabled(0)) multiplexer_1 (
    .in0(_0output), .in1(_1output), .in2(_2output), .in3(_3output), .in4(_4output), .in5(_5output),
    .in6(_6output), .in7(_7output), .in8(_8output), .in9(_9output), .in10(_10output), .in11(_11output),
    .in12(_12output), .in13(_13output), .in14(_14output), .in15(_15output), .in16(_16output),
    .in17(_17output), .in18(_18output), .in19(_19output), .in20(_20output), .in21(_21output),
    .in22(_22output), .in23(_23output), .in24(_24output), .in25(_25output), .in26(_26output),
    .in27(_27output), .in28(_28output), .in29(_29output), .in30(_30output), .in31(_31output), .out(RD1),
    .sel(A1));  // open: en
  Multiplexer #(.select(5), .width(32), .disabled(0)) multiplexer_2 (
    .in0(_0output), .in1(_1output), .in2(_2output), .in3(_3output), .in4(_4output), .in5(_5output),
    .in6(_6output), .in7(_7output), .in8(_8output), .in9(_9output), .in10(_10output), .in11(_11output),
    .in12(_12output), .in13(_13output), .in14(_14output), .in15(_15output), .in16(_16output),
    .in17(_17output), .in18(_18output), .in19(_19output), .in20(_20output), .in21(_21output),
    .in22(_22output), .in23(_23output), .in24(_24output), .in25(_25output), .in26(_26output),
    .in27(_27output), .in28(_28output), .in29(_29output), .in30(_30output), .in31(_31output), .out(RD2),
    .sel(A2));  // open: en
  Demultiplexer #(.select(5), .width(32), .tristate("true")) demultiplexer_1 (
    .out0(_0input), .out1(_1input), .out2(_2input), .out3(_3input), .out4(_4input), .out5(_5input),
    .out6(_6input), .out7(_7input), .out8(_8input), .out9(_9input), .out10(_10input), .out11(_11input),
    .out12(_12input), .out13(_13input), .out14(_14input), .out15(_15input), .out16(_16input),
    .out17(_17input), .out18(_18input), .out19(_19input), .out20(_20input), .out21(_21input),
    .out22(_22input), .out23(_23input), .out24(_24input), .out25(_25input), .out26(_26input),
    .out27(_27input), .out28(_28input), .out29(_29input), .out30(_30input), .out31(_31input), .in(WD3),
    .sel(A3));  // open: en

  // Other names for the same wires on the sheet: clear = reset; clock = clk; enable = WE3
endmodule

module address_changer (
  input  [31:0] in_1,
  output [11:0] out_2
);

  wire [31:0] subtractor_1_out;

  // Probe on in_1
  // Probe on out_2
  Subtractor #(.width(32)) subtractor_1 (
    .a(in_1), .b(32'h3000), .out({subtractor_1_out[31:14], out_2, subtractor_1_out[1:0]}));  // open: bin, bout
endmodule

module Instr_Splitter (
  input  [31:0] in_1,
  output [15:0] immediate,
  output [5:0] func,
  output [4:0] shamt,
  output [4:0] rd,
  output [4:0] rt,
  output [4:0] rs,
  output [5:0] option,
  output [25:0] address
);


  assign address = in_1[25:0];
  assign func = in_1[5:0];
  assign immediate = in_1[15:0];
  assign option = in_1[31:26];
  assign rd = in_1[15:11];
  assign rs = in_1[25:21];
  assign rt = in_1[20:16];
  assign shamt = in_1[10:6];
endmodule

module And_Control_Unit (
  input  [5:0] option,
  input  [5:0] func,
  output ADD,
  output SUB,
  output ORI,
  output LW,
  output SW,
  output BEQ,
  output LUI,
  output J,
  output JAL
);

  wire not_1_out, not_2_out, not_3_out, not_4_out, not_5_out, not_6_out, not_7_out, not_8_out, not_9_out,
       not_10_out, not_11_out, not_12_out;

  not not_1 (not_1_out, option[5]);
  not not_2 (not_2_out, option[4]);
  not not_3 (not_3_out, option[2]);
  not not_4 (not_4_out, option[3]);
  not not_5 (not_5_out, option[1]);
  not not_6 (not_6_out, func[5]);
  not not_7 (not_7_out, option[0]);
  not not_8 (not_8_out, func[3]);
  not not_9 (not_9_out, func[4]);
  and and_1 (ORI, not_1_out, not_2_out, option[3], option[2], not_5_out, option[0]);
  and and_2 (LW, option[5], not_2_out, not_4_out, not_3_out, option[1], option[0]);
  and and_3 (SW, option[5], not_2_out, option[3], not_3_out, option[1], option[0]);
  and and_4 (BEQ, not_1_out, not_2_out, not_4_out, option[2], not_5_out, not_5_out);
  and and_5 (LUI, not_1_out, not_2_out, option[3], option[2], option[1], option[0]);
  and and_6 (J, not_1_out, not_2_out, not_4_out, not_3_out, option[1], not_7_out);
  and and_7 (JAL, not_1_out, not_2_out, not_4_out, not_3_out, option[1], option[0]);
  not not_10 (not_10_out, func[2]);
  not not_11 (not_11_out, func[1]);
  not not_12 (not_12_out, func[0]);
  and and_8 (ADD, not_1_out, not_2_out, not_4_out, not_3_out, not_5_out, not_7_out, func[5], not_9_out, not_8_out, not_10_out, not_11_out, not_12_out);
  and and_9 (SUB, not_1_out, not_2_out, not_4_out, not_3_out, not_5_out, not_7_out, func[5], not_9_out, not_8_out, not_10_out, func[1], not_12_out);

  // Other names for the same wires on the sheet: op0 = option[0]; op1 = option[1]; op2 = option[2]; op3 = option[3];
  //   op4 = option[4]; op5 = option[5]
endmodule

module Or_Control_Unit (
  input  ADD,
  input  SUB,
  input  ORI,
  input  LW,
  input  SW,
  input  BEQ,
  input  LUI,
  input  J,
  input  JAL,
  input  new1,
  input  new2,
  input  new3,
  output MentoReg,
  output ALUsrc,
  output RegDst,
  output RegWrite,
  output imm_extend,
  output Jump,
  output Link,
  output [2:0] ALUop,
  output MemWrite,
  output Branch
);

  wire not_1_out, not_2_out, not_3_out, not_4_out, not_5_out, not_6_out, not_7_out, not_8_out, not_9_out,
       not_10_out, not_11_out, not_12_out;

  not not_1 (not_1_out, ADD);
  not not_2 (not_2_out, SUB);
  not not_3 (not_3_out, ORI);
  not not_4 (not_4_out, LW);
  not not_5 (not_5_out, SW);
  not not_6 (not_6_out, BEQ);
  not not_7 (not_7_out, LUI);
  not not_8 (not_8_out, J);
  not not_9 (not_9_out, JAL);
  not not_10 (not_10_out, new1);
  not not_11 (not_11_out, new2);
  not not_12 (not_12_out, new3);
  or or_1 (ALUop[2], LUI, SUB);
  or or_2 (ALUop[1], SW, LW, SUB, ADD, BEQ);
  or or_3 (ALUop[0], ORI, BEQ);
  or or_4 (ALUsrc, ORI, LW, SW, LUI);
  or or_5 (RegDst, ADD, SUB);
  or or_6 (RegWrite, ADD, SUB, ORI, LW, LUI, JAL);
  or or_7 (imm_extend, BEQ, SW, LW);
  or or_8 (Jump, J, JAL);
  buf or_9 (Link, JAL);  // OR_Gate

  assign Branch = BEQ;
  assign MemWrite = SW;
  assign MentoReg = LW;
endmodule

module ALU (
  input  [31:0] inputA,
  input  [31:0] inputB,
  input  [2:0] option,
  output [31:0] output_calc,
  output output_cmp
);

  wire eq, gt, lt;
  wire [31:0] _16_result, add_result, and_result, or_result, sub_result;

  Adder #(.width(32)) adder_1 (.a(inputA), .b(inputB), .out(add_result));  // open: cin, cout
  Subtractor #(.width(32)) subtractor_1 (.a(inputA), .b(inputB), .out(sub_result));  // open: bin, bout
  Comparator #(.width(32)) comparator_1 (.a(inputA), .b(inputB), .gt(gt), .eq(eq), .lt(lt));
  Shifter #(.width(32)) shifter_1 (.in(inputB), .\dist (5'b10000), .out(_16_result));
  assign and_result = inputA & inputB;  // AND_Gate and_1, 32 bits wide
  assign or_result = inputA | inputB;  // OR_Gate or_1, 32 bits wide
  Multiplexer #(.select(3), .width(32), .disabled(0)) multiplexer_1 (
    .in0(and_result), .in1(or_result), .in2(add_result), .in3(sub_result), .in4(_16_result),
    .in6(sub_result), .out(output_calc), .sel(option));  // open: in5, in7, en
  Multiplexer #(.select(3), .disabled(0)) multiplexer_2 (
    .in0(1'b0), .in1(1'b0), .in2(1'b0), .in3(eq), .in4(1'b0), .in6(1'b0), .out(output_cmp), .sel(option));  // open: in5, in7, en
endmodule

module Comtrol_Unit (
  input  [5:0] option,
  input  [5:0] func,
  output RegWrite,
  output RegDst,
  output ALUsrc,
  output [2:0] ALUop,
  output Branch,
  output MemWrite,
  output MemtoReg,
  output ImmExtend,
  output Jump,
  output Link
);

  wire and_control_unit_1_add, and_control_unit_1_beq, and_control_unit_1_j, and_control_unit_1_jal,
       and_control_unit_1_lui, and_control_unit_1_lw, and_control_unit_1_ori, and_control_unit_1_sub,
       and_control_unit_1_sw;

  Or_Control_Unit or_control_unit_1 (
    .ADD(and_control_unit_1_add), .SUB(and_control_unit_1_sub), .ORI(and_control_unit_1_ori),
    .LW(and_control_unit_1_lw), .SW(and_control_unit_1_sw), .BEQ(and_control_unit_1_beq),
    .LUI(and_control_unit_1_lui), .MentoReg(MemtoReg), .MemWrite(MemWrite), .Branch(Branch), .ALUop(ALUop),
    .ALUsrc(ALUsrc), .RegDst(RegDst), .RegWrite(RegWrite), .imm_extend(ImmExtend), .Jump(Jump),
    .J(and_control_unit_1_j), .JAL(and_control_unit_1_jal), .Link(Link));  // open: new1, new2, new3
  And_Control_Unit and_control_unit_1 (
    .option(option), .func(func), .ADD(and_control_unit_1_add), .SUB(and_control_unit_1_sub),
    .ORI(and_control_unit_1_ori), .LW(and_control_unit_1_lw), .SW(and_control_unit_1_sw),
    .BEQ(and_control_unit_1_beq), .LUI(and_control_unit_1_lui), .J(and_control_unit_1_j),
    .JAL(and_control_unit_1_jal));
endmodule
