// Logisim project RS_latch.circ as structural Verilog: 3 circuits, main circuit RS_latch
module RS_latch (
  input  R,
  input  S,
  output Q,
  output nQ
);

  wire or_1_out, or_2_out;

  or or_1 (or_1_out, R, nQ);
  or or_2 (or_2_out, Q, S);
  not not_1 (Q, or_1_out);
  not not_2 (nQ, or_2_out);
endmodule

module D_latch (
  input  clock,
  input  D,
  output Q,
  output nQ
);

  wire and_1_out, and_2_out, not_1_out;

  not not_1 (not_1_out, D);
  and and_1 (and_1_out, not_1_out, clock);
  and and_2 (and_2_out, D, clock);
  RS_latch rs_latch_1 (.R(and_1_out), .S(and_2_out), .Q(Q), .nQ(nQ));
endmodule

module D_Flip_Flop (
  input  clock,
  input  D,
  output Q,
  output nQ
);

  wire d_latch_1_q, not_1_out;

  not not_1 (not_1_out, clock);
  D_latch d_latch_1 (.clock(not_1_out), .D(D), .Q(d_latch_1_q));  // open: nQ
  D_latch d_latch_2 (.clock(clock), .D(d_latch_1_q), .Q(Q), .nQ(nQ));
endmodule
