// Logisim project clock_2^i.circ as structural Verilog: 1 circuit, main circuit main
module main (
  input  in_1,
  input  in_2,
  input  in_3
);

  wire comparator_1_eq;
  wire [7:0] multiplexer_1_out, multiplier_1_out, register_1_q;

  Multiplexer #(.width(8)) multiplexer_1 (
    .in0(multiplier_1_out), .in1(8'h1), .out(multiplexer_1_out), .sel(comparator_1_eq));  // open: en
  // Probe on comparator_1_eq
  // Probe on multiplexer_1_out
  Register register_1 (.D(multiplexer_1_out), .en(in_1), .Q(register_1_q), .clk(in_2), .clr(in_3));
  // Probe on register_1_q
  Multiplier multiplier_1 (.a(8'h2), .b(register_1_q), .out(multiplier_1_out));  // open: cin, cout
  Comparator comparator_1 (.a(multiplier_1_out), .b({8{1'b0}}), .eq(comparator_1_eq));  // open: gt, lt
endmodule
