// Logisim project fib.circ as structural Verilog: 3 circuits, main circuit main
module main (
  input  [2:0] in_1,
  output [3:0] out_2
);

  wire clock_1_out, frozen;
  wire [3:0] \计算逻辑_1_output_now ;

  Clock clock_1 (.out(clock_1_out));
  \计数逻辑  \u_计数逻辑_1  (.\input (in_1), .clock(clock_1_out), .reset(1'b0), .frozen(frozen));
  \计算逻辑  \u_计算逻辑_1  (.reset(1'b0), .clock(clock_1_out), .output_now(\计算逻辑_1_output_now ), .frozen(frozen));
  Multiplexer #(.width(4)) multiplexer_1 (
    .in0(4'b0000), .in1(\计算逻辑_1_output_now ), .out(out_2), .sel(frozen));  // open: en
endmodule

module \计算逻辑  (
  input  reset,
  input  clock,
  input  frozen,
  output [3:0] output_now
);

  wire frozen_t, init;
  wire [3:0] adder_1_out, multiplexer_1_out, pre;

  Counter #(.width(1), .max('h1), .ongoal("stay")) counter_1 (
    .Q(init), .clk(clock), .clr(reset));  // open: load, D, count, carry
  not not_1 (frozen_t, frozen);
  Multiplexer #(.width(4)) multiplexer_1 (
    .in0(4'b0001), .in1(output_now), .out(multiplexer_1_out), .sel(init));  // open: en
  Adder #(.width(4)) adder_1 (.a(pre), .b(output_now), .out(adder_1_out));  // open: cin, cout
  Register #(.width(4)) u_pre (.D(multiplexer_1_out), .en(frozen_t), .Q(pre), .clk(clock), .clr(reset));
  Register #(.width(4)) now (.D(adder_1_out), .en(frozen_t), .Q(output_now), .clk(clock), .clr(reset));
  // Probe on pre
  // Probe on output_now

  // Other names for the same wires on the sheet: now[3:0] = output_now
endmodule

module \计数逻辑  (
  input  [2:0] \input ,
  input  clock,
  input  reset,
  output frozen
);

  wire [3:0] bit_extender_1_out, counter_1_q;

  Counter #(.width(4), .max('hf), .ongoal("stay")) counter_1 (
    .Q(counter_1_q), .clk(clock), .clr(reset));  // open: load, D, count, carry
  // Probe on counter_1_q
  assign bit_extender_1_out = {{1{1'b0}}, \input };  // Bit_Extender bit_extender_1
  // Probe on bit_extender_1_out
  Comparator #(.width(4), .mode("unsigned")) comparator_1 (
    .a(counter_1_q), .b(bit_extender_1_out), .gt(frozen));  // open: eq, lt
endmodule
