// Logisim project fsm.circ as structural Verilog: 3 circuits, main circuit fsm
module fsm (
  input  [1:0] Input,
  input  reset,
  output \output 
);

  wire clock_1_out;
  wire [1:0] multiplexer_1_out, register_1_q, \状态转移_1_下一状态 ;

  \状态转移  \u_状态转移_1  (.\当前状态 (register_1_q), .Input(Input), .\下一状态 (\状态转移_1_下一状态 ));
  Multiplexer #(.width(2)) multiplexer_1 (
    .in0(\状态转移_1_下一状态 ), .in1(2'b00), .out(multiplexer_1_out), .sel(reset));  // open: en
  Clock clock_1 (.out(clock_1_out));
  Register #(.width(2)) register_1 (.D(multiplexer_1_out), .Q(register_1_q), .clk(clock_1_out));  // open: en, clr
  // Probe on register_1_q
  \状态输出  \u_状态输出_1  (.\当前状态 (register_1_q), .Input(Input), .\output (\output ));
endmodule

module \状态转移  (
  input  [1:0] \当前状态 ,
  input  [1:0] Input,
  output [1:0] \下一状态 
);

  wire and_1_out, and_2_out, and_3_out, and_4_out, not_1_out, not_2_out, not_3_out, not_4_out, not_5_out,
       not_6_out, not_7_out;

  not not_1 (not_1_out, \当前状态 [1]);
  not not_2 (not_2_out, Input[0]);
  not not_3 (not_3_out, \当前状态 [0]);
  not not_4 (not_4_out, Input[0]);
  not not_5 (not_5_out, Input[1]);
  not not_6 (not_6_out, \当前状态 [0]);
  not not_7 (not_7_out, Input[0]);
  and and_1 (and_1_out, not_1_out, \当前状态 [0], not_2_out);
  and and_2 (and_2_out, \当前状态 [1], not_3_out, not_4_out);
  and and_3 (and_3_out, not_5_out, Input[0]);
  and and_4 (and_4_out, \当前状态 [1], not_6_out, not_7_out);
  or or_1 (\下一状态 [1], and_1_out, and_2_out);
  or or_2 (\下一状态 [0], and_3_out, and_4_out);
endmodule

module \状态输出  (
  input  [1:0] \当前状态 ,
  input  [1:0] Input,
  output \output 
);

  wire and_1_out, and_2_out, and_3_out, and_4_out, not_1_out, not_2_out, not_3_out, not_4_out, not_5_out,
       not_6_out, not_7_out;
  wire [1:0] or_2_out;

  not not_1 (not_1_out, \当前状态 [1]);
  not not_2 (not_2_out, Input[0]);
  not not_3 (not_3_out, \当前状态 [0]);
  not not_4 (not_4_out, Input[0]);
  not not_5 (not_5_out, Input[1]);
  not not_6 (not_6_out, \当前状态 [0]);
  not not_7 (not_7_out, Input[0]);
  and and_1 (and_1_out, not_1_out, \当前状态 [0], not_2_out);
  and and_2 (and_2_out, \当前状态 [1], not_3_out, not_4_out);
  and and_3 (and_3_out, not_5_out, Input[0]);
  and and_4 (and_4_out, \当前状态 [1], not_6_out, not_7_out);
  or or_1 (or_2_out[1], and_1_out, and_2_out);
  or or_2 (or_2_out[0], and_3_out, and_4_out);
  Comparator #(.width(2), .mode("unsigned")) comparator_1 (.a(or_2_out), .b(2'b11), .eq(\output ));  // open: gt, lt
endmodule
