// Logisim project ftoi.circ as structural Verilog: 3 circuits, main circuit ftoi
module ftoi (
  input  [15:0] Input,
  output [31:0] out_2
);

  wire comparator_1_eq, comparator_2_eq;
  wire [4:0] E;
  wire [10:10] M;
  wire [15:0] calc_int_1_out_3;
  wire [31:0] abs, adder_1_out, multiplexer_2_out, not_1_out;

  // Probe on Input[14:10]
  // Probe on 5'b01111
  // Probe on E
  Subtractor #(.width(5)) subtractor_1 (.a(Input[14:10]), .b(5'b01111), .out(E));  // open: bin, bout
  Comparator #(.width(5)) comparator_1 (.a(Input[14:10]), .b({5{1'b0}}), .eq(comparator_1_eq));  // open: gt, lt
  Multiplexer multiplexer_1 (.in0(1'b1), .in1(1'b0), .out(M[10]), .sel(comparator_1_eq));  // open: en
  // Probe on {M[10], Input[9:0]}
  calc_int calc_int_1 (.M({M[10], Input[9:0]}), .E(E), .out_3(calc_int_1_out_3));
  assign abs = {{16{1'b0}}, calc_int_1_out_3};  // Bit_Extender bit_extender_1
  assign not_1_out = ~abs;  // NOT_Gate not_1, 32 bits wide
  Adder #(.width(32)) adder_1 (.a(not_1_out), .b(32'h1), .out(adder_1_out));  // open: cin, cout
  Multiplexer #(.width(32)) multiplexer_2 (
    .in0(abs), .in1(adder_1_out), .out(multiplexer_2_out), .sel(Input[15]));  // open: en
  Multiplexer #(.width(32)) multiplexer_3 (
    .in0(multiplexer_2_out), .in1({32{1'b0}}), .out(out_2), .sel(comparator_2_eq));  // open: en
  Comparator #(.width(5)) comparator_2 (.a(Input[14:10]), .b({5{1'b1}}), .eq(comparator_2_eq));  // open: gt, lt

  // Other names for the same wires on the sheet: exponent[4:0] = Input[14:10]; S = Input[15]; frac[9:0] = Input[9:0];
  //   M[9:0] = Input[9:0]
endmodule

module calc_int (
  input  [10:0] M,
  input  [4:0] E,
  output [15:0] out_3
);

  wire less0;
  wire [14:0] n15bithigh_1_out_3;
  wire [15:0] _1_15, adder_1_out, bit_extender_1_out, bit_extender_2_out, bit_extender_3_out, shifter_2_out;

  // Probe on E
  // Probe on bit_extender_1_out
  assign bit_extender_1_out = {{5{1'b0}}, M};  // Bit_Extender bit_extender_1
  Comparator #(.width(5)) comparator_1 (.a(E), .b({5{1'b0}}), .lt(less0));  // open: gt, eq
  // Probe on _1_15
  Shifter #(.width(16)) shifter_1 (.in(bit_extender_1_out), .\dist (4'b0101), .out(_1_15));
  _15bitHigh u_15bithigh_1 (._15bit(_1_15[14:0]), .X(E[3:0]), .out_3(n15bithigh_1_out_3));
  assign bit_extender_2_out = {{1{1'b0}}, n15bithigh_1_out_3};  // Bit_Extender bit_extender_2
  assign bit_extender_3_out = {{15{1'b0}}, _1_15[15]};  // Bit_Extender bit_extender_3
  Shifter #(.width(16)) shifter_2 (.in(bit_extender_3_out), .\dist (E[3:0]), .out(shifter_2_out));
  Adder #(.width(16)) adder_1 (.a(bit_extender_2_out), .b(shifter_2_out), .out(adder_1_out));  // open: cin, cout
  Multiplexer #(.width(16)) multiplexer_1 (.in0(adder_1_out), .in1({16{1'b0}}), .out(out_3), .sel(less0));  // open: en

  // Other names for the same wires on the sheet: 小数部分[14:0] = _1_15[14:0]; 整数部分 = _1_15[15]
endmodule

module _15bitHigh (
  input  [14:0] _15bit,
  input  [3:0] X,
  output [14:0] out_3
);

  wire [3:0] subtractor_1_out;

  Subtractor #(.width(4)) subtractor_1 (.a(4'b1111), .b(X), .out(subtractor_1_out));  // open: bin, bout
  Shifter #(.width(15), .shift("lr")) shifter_1 (.in(_15bit), .\dist (subtractor_1_out), .out(out_3));
  // Probe on out_3
endmodule
