// Logisim project grf.circ as structural Verilog: 1 circuit, main circuit grf
module grf (
  input  clk,
  input  reset,
  input  WE,
  input  [31:0] WD,
  input  [4:0] A3,
  input  [4:0] A1,
  input  [4:0] A2,
  output [31:0] RD1,
  output [31:0] RD2
);

  wire [31:0] _0input, _0output, _1input, _1output, _2input, _2output, _3input, _3output, _4input, _4output,
       _5input, _5output, _6input, _6output, _7input, _7output, _8input, _8output, _9input, _9output,
       _10input, _10output, _11input, _11output, _12input, _12output, _13input, _13output, _14input,
       _14output, _15input, _15output, _16input, _16output, _17input, _17output, _18input, _18output,
       _19input, _19output, _20input, _20output, _21input, _21output, _22input, _22output, _23input,
       _23output, _24input, _24output, _25input, _25output, _26input, _26output, _27input, _27output,
       _28input, _28output, _29input, _29output, _30input, _30output, _31input, _31output;

  Register #(.width(32)) register_1 (.D(_0input), .en(1'b0), .Q(_0output), .clk(clk), .clr(reset));
  Register #(.width(32)) register_2 (.D(_1input), .en(WE), .Q(_1output), .clk(clk), .clr(reset));
  Register #(.width(32)) register_3 (.D(_2input), .en(WE), .Q(_2output), .clk(clk), .clr(reset));
  Register #(.width(32)) register_4 (.D(_3input), .en(WE), .Q(_3output), .clk(clk), .clr(reset));
  Register #(.width(32)) register_5 (.D(_4input), .en(WE), .Q(_4output), .clk(clk), .clr(reset));
  Register #(.width(32)) register_6 (.D(_5input), .en(WE), .Q(_5output), .clk(clk), .clr(reset));
  Register #(.width(32)) register_7 (.D(_6input), .en(WE), .Q(_6output), .clk(clk), .clr(reset));
  Register #(.width(32)) register_8 (.D(_7input), .en(WE), .Q(_7output), .clk(clk), .clr(reset));
  Register #(.width(32)) register_9 (.D(_8input), .en(WE), .Q(_8output), .clk(clk), .clr(reset));
  Register #(.width(32)) register_10 (.D(_9input), .en(WE), .Q(_9output), .clk(clk), .clr(reset));
  Register #(.width(32)) register_11 (.D(_10input), .en(WE), .Q(_10output), .clk(clk), .clr(reset));
  Register #(.width(32)) register_12 (.D(_11input), .en(WE), .Q(_11output), .clk(clk), .clr(reset));
  Register #(.width(32)) register_13 (.D(_12input), .en(WE), .Q(_12output), .clk(clk), .clr(reset));
  Register #(.width(32)) register_14 (.D(_13input), .en(WE), .Q(_13output), .clk(clk), .clr(reset));
  Register #(.width(32)) register_15 (.D(_14input), .en(WE), .Q(_14output), .clk(clk), .clr(reset));
  Register #(.width(32)) register_16 (.D(_15input), .en(WE), .Q(_15output), .clk(clk), .clr(reset));
  Register #(.width(32)) register_17 (.D(_16input), .en(WE), .Q(_16output), .clk(clk), .clr(reset));
  Register #(.width(32)) register_18 (.D(_17input), .en(WE), .Q(_17output), .clk(clk), .clr(reset));
  Register #(.width(32)) register_19 (.D(_18input), .en(WE), .Q(_18output), .clk(clk), .clr(reset));
  Register #(.width(32)) register_20 (.D(_19input), .en(WE), .Q(_19output), .clk(clk), .clr(reset));
  Register #(.width(32)) register_21 (.D(_20input), .en(WE), .Q(_20output), .clk(clk), .clr(reset));
  Register #(.width(32)) register_22 (.D(_21input), .en(WE), .Q(_21output), .clk(clk), .clr(reset));
  Register #(.width(32)) register_23 (.D(_22input), .en(WE), .Q(_22output), .clk(clk), .clr(reset));
  Register #(.width(32)) register_24 (.D(_23input), .en(WE), .Q(_23output), .clk(clk), .clr(reset));
  Register #(.width(32)) register_25 (.D(_24input), .en(WE), .Q(_24output), .clk(clk), .clr(reset));
  Register #(.width(32)) register_26 (.D(_25input), .en(WE), .Q(_25output), .clk(clk), .clr(reset));
  Register #(.width(32)) register_27 (.D(_26input), .en(WE), .Q(_26output), .clk(clk), .clr(reset));
  Register #(.width(32)) register_28 (.D(_27input), .en(WE), .Q(_27output), .clk(clk), .clr(reset));
  Register #(.width(32)) register_29 (.D(_28input), .en(WE), .Q(_28output), .clk(clk), .clr(reset));
  Register #(.width(32)) register_30 (.D(_29input), .en(WE), .Q(_29output), .clk(clk), .clr(reset));
  Register #(.width(32)) register_31 (.D(_30input), .en(WE), .Q(_30output), .clk(clk), .clr(reset));
  Register #(.width(32)) register_32 (.D(_31input), .en(WE), .Q(_31output), .clk(clk), .clr(reset));
  Multiplexer #(.select(5), .width(32), .disabled(0)) multiplexer_1 (
    .in0(_0output), .in1(_1output), .in2(_2output), .in3(_3output), .in4(_4output), .in5(_5output),
    .in6(_6output), .in7(_7output), .in8(_8output), .in9(_9output), .in10(_10output), .in11(_11output),
    .in12(_12output), .in13(_13output), .in14(_14output), .in15(_15output), .in16(_16output),
    .in17(_17output), .in18(_18output), .in19(_19output), .in20(_20output), .in21(_21output),
    .in22(_22output), .in23(_23output), .in24(_24output), .in25(_25output), .in26(_26output),
    .in27(_27output), .in28(_28output), .in29(_29output), .in30(_30output), .in31(_31output), .out(RD1),
    .sel(A1));  // open: en
  Multiplexer #(.select(5), .width(32), .disabled(0)) multiplexer_2 (
    .in0(_0output), .in1(_1output), .in2(_2output), .in3(_3output), .in4(_4output), .in5(_5output),
    .in6(_6output), .in7(_7output), .in8(_8output), .in9(_9output), .in10(_10output), .in11(_11output),
    .in12(_12output), .in13(_13output), .in14(_14output), .in15(_15output), .in16(_16output),
    .in17(_17output), .in18(_18output), .in19(_19output), .in20(_20output), .in21(_21output),
    .in22(_22output), .in23(_23output), .in24(_24output), .in25(_25output), .in26(_26output),
    .in27(_27output), .in28(_28output), .in29(_29output), .in30(_30output), .in31(_31output), .out(RD2),
    .sel(A2));  // open: en
  Demultiplexer #(.select(5), .width(32), .tristate("true")) demultiplexer_1 (
    .out0(_0input), .out1(_1input), .out2(_2input), .out3(_3input), .out4(_4input), .out5(_5input),
    .out6(_6input), .out7(_7input), .out8(_8input), .out9(_9input), .out10(_10input), .out11(_11input),
    .out12(_12input), .out13(_13input), .out14(_14input), .out15(_15input), .out16(_16input),
    .out17(_17input), .out18(_18input), .out19(_19input), .out20(_20input), .out21(_21input),
    .out22(_22input), .out23(_23input), .out24(_24input), .out25(_25input), .out26(_26input),
    .out27(_27input), .out28(_28input), .out29(_29input), .out30(_30input), .out31(_31input), .in(WD),
    .sel(A3));  // open: en

  // Other names for the same wires on the sheet: clear = reset; clock = clk; enable = WE
endmodule
