// Logisim project navigation.circ as structural Verilog: 2 circuits, main circuit navigation
module navigation (
  input  [1:0] dir,
  input  clk,
  input  reset,
  output hit,
  output arrive
);

  wire \状态转移_1_arrive , \状态转移_1_hit ;
  wire [2:0] \状态储存_q , \状态转移_1_下一状态 ;

  \状态转移  \u_状态转移_1  (
    .\当前状态 (\状态储存_q ), .dir(dir), .\下一状态 (\状态转移_1_下一状态 ), .hit(\状态转移_1_hit ), .arrive(\状态转移_1_arrive ));
  Register #(.width(3)) \u_状态储存  (.D(\状态转移_1_下一状态 ), .Q(\状态储存_q ), .clk(clk), .clr(reset));  // open: en
  Register #(.width(1)) u_hit (.D(\状态转移_1_hit ), .Q(hit), .clk(clk), .clr(reset));  // open: en
  Register #(.width(1)) u_arrive (.D(\状态转移_1_arrive ), .Q(arrive), .clk(clk), .clr(reset));  // open: en
  // Probe on \状态储存_q 
endmodule

module \状态转移  (
  input  [2:0] \当前状态 ,
  input  [1:0] dir,
  output [2:0] \下一状态 ,
  output hit,
  output arrive
);

  wire and_1_out, and_2_out, and_3_out, and_4_out, and_5_out, and_6_out, and_7_out, and_8_out, and_9_out,
       and_10_out, and_11_out, and_12_out, and_13_out, and_14_out, and_15_out, and_16_out, and_17_out,
       and_18_out, and_19_out, and_20_out, not_1_out, not_2_out, not_3_out, not_4_out, not_5_out, not_6_out,
       not_7_out, not_8_out, not_9_out, not_10_out, not_11_out, not_12_out, not_13_out, not_14_out,
       not_15_out, not_16_out, not_17_out, not_18_out, not_19_out, not_20_out, not_21_out, not_22_out,
       not_23_out, not_24_out, not_25_out, not_26_out, not_27_out, not_28_out, not_29_out, not_30_out,
       not_31_out, not_32_out;

  not not_1 (not_1_out, \当前状态 [0]);
  not not_2 (not_2_out, dir[1]);
  not not_3 (not_3_out, dir[0]);
  not not_4 (not_4_out, dir[1]);
  not not_5 (not_5_out, \当前状态 [1]);
  not not_6 (not_6_out, dir[1]);
  not not_7 (not_7_out, dir[1]);
  not not_8 (not_8_out, dir[0]);
  not not_9 (not_9_out, \当前状态 [0]);
  not not_10 (not_10_out, dir[1]);
  not not_11 (not_11_out, \当前状态 [0]);
  not not_12 (not_12_out, dir[0]);
  not not_13 (not_13_out, \当前状态 [2]);
  not not_14 (not_14_out, \当前状态 [1]);
  not not_15 (not_15_out, dir[1]);
  not not_16 (not_16_out, dir[0]);
  not not_17 (not_17_out, dir[0]);
  not not_18 (not_18_out, \当前状态 [2]);
  not not_19 (not_19_out, \当前状态 [0]);
  not not_20 (not_20_out, dir[1]);
  not not_21 (not_21_out, \当前状态 [2]);
  not not_22 (not_22_out, \当前状态 [1]);
  not not_23 (not_23_out, \当前状态 [0]);
  not not_24 (not_24_out, \当前状态 [2]);
  not not_25 (not_25_out, \当前状态 [0]);
  not not_26 (not_26_out, dir[0]);
  not not_27 (not_27_out, dir[1]);
  not not_28 (not_28_out, dir[0]);
  not not_29 (not_29_out, \当前状态 [0]);
  not not_30 (not_30_out, dir[1]);
  not not_31 (not_31_out, dir[0]);
  not not_32 (not_32_out, dir[1]);
  and and_1 (and_1_out, \当前状态 [1], not_1_out, not_2_out, not_3_out);
  and and_2 (and_2_out, \当前状态 [1], \当前状态 [0], not_4_out, dir[0]);
  and and_3 (and_3_out, not_5_out, \当前状态 [0], not_6_out);
  and and_4 (and_4_out, \当前状态 [0], not_7_out, not_8_out);
  and and_5 (and_5_out, \当前状态 [1], not_9_out, not_10_out, dir[0]);
  and and_6 (and_6_out, \当前状态 [1], not_11_out, dir[1], not_12_out);
  and and_7 (and_7_out, \当前状态 [1], \当前状态 [0], dir[1], dir[0]);
  and and_8 (and_8_out, not_13_out, not_14_out, not_15_out, not_16_out);
  and and_9 (and_9_out, \当前状态 [0], dir[1], dir[0]);
  and and_10 (and_10_out, \当前状态 [1], dir[1], dir[0]);
  and and_11 (and_11_out, \当前状态 [1], \当前状态 [0], not_17_out);
  and and_12 (and_12_out, not_18_out, not_19_out, not_20_out, dir[0]);
  and and_13 (and_13_out, not_21_out, not_22_out, not_23_out, dir[1]);
  and and_14 (and_14_out, not_24_out, not_25_out, dir[1], not_26_out);
  and and_15 (and_15_out, \当前状态 [0], dir[1], dir[0]);
  and and_16 (and_16_out, \当前状态 [1], \当前状态 [0], not_27_out, not_28_out);
  and and_17 (and_17_out, \当前状态 [1], not_29_out, not_30_out, not_31_out);
  and and_18 (and_18_out, \当前状态 [1], \当前状态 [0], not_32_out, dir[0]);
  and and_19 (and_19_out, \当前状态 [2], \当前状态 [0]);
  and and_20 (and_20_out, \当前状态 [2], \当前状态 [1]);
  or or_1 (\下一状态 [2], and_1_out, and_2_out);
  or or_2 (\下一状态 [1], and_3_out, and_4_out, and_5_out, and_6_out, and_7_out);
  or or_3 (\下一状态 [0], and_8_out, and_9_out, and_10_out, and_11_out);
  or or_4 (hit, and_12_out, and_13_out, and_14_out, and_15_out, and_16_out);
  or or_5 (arrive, and_17_out, and_18_out, and_19_out, and_20_out);
endmodule
