// Logisim project re_2^nmod5.circ as structural Verilog: 3 circuits, main circuit mod5
module mod5 (
  input  Input,
  output out_2,
  output out_3,
  output out_4,
  output out_5,
  output out_6
);

  wire clock_1_out;
  wire [1:0] register_1_q, \状态转移_1_out_3 ;

  \状态转移  \u_状态转移_1  (.C(register_1_q), .Input(Input), .out_3(\状态转移_1_out_3 ));
  Register #(.width(2)) register_1 (.D(\状态转移_1_out_3 ), .Q(register_1_q), .clk(clock_1_out));  // open: en, clr
  Clock clock_1 (.out(clock_1_out));
  \状态输出  \u_状态输出_1  (.C(register_1_q), .Input(Input), .s0(out_2), .s1(out_3), .s2(out_4), .s3(out_5), .s4(out_6));
endmodule

module \状态转移  (
  input  [1:0] C,
  input  Input,
  output [1:0] out_3
);

  wire nand_1_out, nand_2_out, nand_3_out, nand_4_out, nand_5_out, nand_6_out, nand_7_out, nand_8_out,
       nand_9_out, nand_10_out, nand_11_out, nand_12_out, nand_13_out;

  nand nand_1 (nand_1_out, C[1], C[1]);
  nand nand_2 (nand_2_out, C[1], C[1]);
  nand nand_3 (nand_3_out, C[0], C[0]);
  nand nand_4 (nand_4_out, C[1], C[1]);
  nand nand_5 (nand_5_out, Input, Input);
  nand nand_6 (nand_6_out, C[0], C[0]);
  nand nand_7 (nand_7_out, Input, Input);
  nand nand_8 (nand_8_out, nand_1_out, Input);
  nand nand_9 (nand_9_out, nand_2_out, C[0]);
  nand nand_10 (nand_10_out, C[1], nand_3_out);
  nand nand_11 (nand_11_out, nand_4_out, C[0], nand_5_out);
  nand nand_12 (nand_12_out, C[1], nand_6_out, nand_7_out);
  nand nand_13 (nand_13_out, C[1], C[0], Input);
  nand nand_14 (out_3[1], nand_8_out, nand_9_out, nand_10_out);
  nand nand_15 (out_3[0], nand_11_out, nand_12_out, nand_13_out);
endmodule

module \状态输出  (
  input  [1:0] C,
  input  Input,
  output s0,
  output s1,
  output s2,
  output s3,
  output s4
);

  wire nand_1_out, nand_2_out, nand_3_out, nand_4_out, nand_5_out, nand_6_out, nand_7_out, nand_8_out,
       nand_9_out, nand_10_out, nand_11_out, nand_12_out, nand_13_out, nand_14_out, nand_15_out, nand_16_out,
       nand_17_out, nand_18_out, nand_19_out, nand_20_out;

  nand nand_1 (nand_1_out, C[1], C[1]);
  nand nand_2 (nand_2_out, C[0], C[0]);
  nand nand_3 (nand_3_out, Input, Input);
  nand nand_4 (nand_4_out, Input, Input);
  nand nand_5 (nand_5_out, C[1], C[1]);
  nand nand_6 (nand_6_out, C[0], C[0]);
  nand nand_7 (nand_7_out, C[1], C[1]);
  nand nand_8 (nand_8_out, C[0], C[0]);
  nand nand_9 (nand_9_out, C[1], C[1]);
  nand nand_10 (nand_10_out, Input, Input);
  nand nand_11 (nand_11_out, C[0], C[0]);
  nand nand_12 (nand_12_out, Input, Input);
  nand nand_13 (nand_13_out, nand_1_out, nand_2_out, nand_3_out);
  nand nand_14 (nand_14_out, C[1], C[0], nand_4_out);
  nand nand_15 (nand_15_out, nand_5_out, nand_6_out, Input);
  nand nand_16 (nand_16_out, C[1], C[0], Input);
  nand nand_17 (nand_17_out, nand_7_out, C[0], Input);
  nand nand_18 (nand_18_out, C[1], nand_8_out, Input);
  nand nand_19 (nand_19_out, nand_9_out, C[0], nand_10_out);
  nand nand_20 (nand_20_out, C[1], nand_11_out, nand_12_out);
  nand nand_21 (s1, nand_13_out, nand_14_out);
  nand nand_22 (s2, nand_15_out, nand_16_out);
  nand nand_23 (s3, nand_17_out, nand_18_out);
  nand nand_24 (s4, nand_19_out, nand_20_out);

  assign s0 = 1'b0;
endmodule
