// Logisim project re_fib.circ as structural Verilog: 3 circuits, main circuit main
module main (
  input  [2:0] in_1,
  output [3:0] out_2
);

  wire clk, frozen;
  wire [3:0] \计算电路_1_output ;

  Clock clock_1 (.out(clk));
  \计数电路  \u_计数电路  (.Input(in_1), .reset(1'b0), .clk(clk), .\output (frozen));
  \计算电路  \u_计算电路_1  (.clk(clk), .reset(1'b0), .frozen(frozen), .\output (\计算电路_1_output ));
  Multiplexer #(.width(4)) multiplexer_1 (.in0(4'b0000), .in1(\计算电路_1_output ), .out(out_2), .sel(frozen));  // open: en
endmodule

module \计数电路  (
  input  [2:0] Input,
  input  reset,
  input  clk,
  output \output 
);

  wire [3:0] bit_extender_1_out, counter_1_q;

  assign bit_extender_1_out = {{1{1'b0}}, Input};  // Bit_Extender bit_extender_1
  Counter #(.width(4), .max('hf), .ongoal("stay")) counter_1 (
    .Q(counter_1_q), .clk(clk), .clr(reset));  // open: load, D, count, carry
  Comparator #(.width(4), .mode("unsigned")) comparator_1 (
    .a(bit_extender_1_out), .b(counter_1_q), .lt(\output ));  // open: gt, eq
endmodule

module \计算电路  (
  input  clk,
  input  reset,
  input  frozen,
  output [3:0] \output 
);

  wire enable, init;
  wire [3:0] adder_1_out, multiplexer_1_out, multiplexer_2_out, pre_out;

  not not_1 (enable, frozen);
  Counter #(.width(1), .max('h1), .ongoal("stay")) counter_1 (
    .Q(init), .clk(clk), .clr(reset));  // open: load, D, count, carry
  Adder #(.width(4)) adder_1 (.a(\output ), .b(pre_out), .out(adder_1_out));  // open: cin, cout
  Multiplexer #(.width(4)) multiplexer_1 (
    .in0(4'b0001), .in1(\output ), .out(multiplexer_1_out), .sel(init));  // open: en
  Multiplexer #(.width(4)) multiplexer_2 (
    .in0(4'b0000), .in1(adder_1_out), .out(multiplexer_2_out), .sel(init));  // open: en
  Register #(.width(4)) pre (.D(multiplexer_1_out), .en(enable), .Q(pre_out), .clk(clk), .clr(reset));
  Register #(.width(4)) now (.D(multiplexer_2_out), .en(enable), .Q(\output ), .clk(clk), .clr(reset));

  // Other names for the same wires on the sheet: clock = clk; now_out[3:0] = \output 
endmodule
